# Fritzing sketch Sketch (saved by Fritzing 0.9.3b)
breadboards: 1

parts:
  R1 = Rotary Potentiometer (Small) [maximum_resistance=100kΩ package=THT]
  Parça1 = Arduino Ethernet Shield (Rev3)
  S1 = Pushbutton [package="[THT]"]
  S2 = Pushbutton [package="[THT]"]
  S3 = Pushbutton [package="[THT]"]
  S4 = Pushbutton [package="[THT]"]
  S5 = Pushbutton [package="[THT]"]
  LED1 = LED - 5mm [color="Red (633nm)" package="5 mm [THT]"]
  LED2 = LED - 5mm [color="Yellow (595nm)" package="5 mm [THT]"]
  R2 = Resistor [tolerance=±5% resistance=220 package=THT]
  R3 = Resistor [tolerance=±5% resistance=220 package=THT]

nets:
  N1: R1.leg1, LED1.cathode, LED2.cathode
  N2: R1.wiper, Parça1.A5/SCL
  N3: R1.leg2, S1.Pin_1, S1.Pin_2, S2.Pin_1, S2.Pin_2, S3.Pin_1, S3.Pin_2, S4.Pin_1, S4.Pin_2, S5.Pin_1, S5.Pin_2
  N4: Parça1.ETH_CS, R2.Pin_1
  N5: Parça1.PWM_D11, R3.Pin_1
  N6: Parça1.PWM_D3, S1.Pin_3, S1.Pin_4
  N7: Parça1.SDCS, S2.Pin_3, S2.Pin_4
  N8: Parça1.PWM_D5, S3.Pin_3, S3.Pin_4
  N9: Parça1.PWM_D6, S4.Pin_3, S4.Pin_4
  N10: Parça1.D7, S5.Pin_3, S5.Pin_4
  N11: LED1.anode, R2.Pin_0
  N12: LED2.anode, R3.Pin_0
